# Fritzing sketch thermostat (saved by Fritzing 0.9.0b)
breadboards: 1

parts:
  Adafruit_HUZZAH_ESP8266_Breakout1 = Adafruit HUZZAH ESP8266 Breakout [part_number=2471]
  U1 = TMP36 [package=to-92-kit]
  R1 = Resistor [tolerance=±5% resistance=220 package=THT]  # not connected
  LED1 = LED - 5mm [color="Red (633nm)" package="5 mm [THT]"]
  K1 = Relay [part_number=FRS1B-S package=THT]

nets:
  GND: Adafruit_HUZZAH_ESP8266_Breakout1.GND, U1.GND, LED1.anode, K1.COIL1, K1.COIL2
  N1: Adafruit_HUZZAH_ESP8266_Breakout1.A, U1.VOUT
  N2: Adafruit_HUZZAH_ESP8266_Breakout1.3V, U1.VCC
  N3: K1.A, K1.B
  N4: K1.C1, K1.C2
